// Logisim project 201413283_김재훈_2.circ as structural Verilog: 2 circuits, main circuit main
module main (
  input  I2,
  input  I1,
  input  I0,
  output O0,
  output O1,
  output O2,
  output O3,
  output O4,
  output O5,
  output O6,
  output O7
);

  wire not_1_out, not_2_out, not_3_out;

  not not_1 (not_1_out, I2);
  not not_2 (not_2_out, I1);
  not not_3 (not_3_out, I0);
  and and_1 (O0, I2, I1, I0);
  and and_2 (O1, I2, I1, not_3_out);
  and and_3 (O2, I2, not_2_out, I0);
  and and_4 (O3, I2, not_2_out, not_3_out);
  and and_5 (O4, not_1_out, I1, I0);
  and and_6 (O5, not_1_out, I1, not_3_out);
  and and_7 (O6, not_1_out, not_2_out, I0);
  and and_8 (O7, not_1_out, not_2_out, not_3_out);
endmodule

module _2 (
  input  I3,
  input  I2,
  input  I1,
  input  I0,
  output Y1,
  output Y2,
  output V
);

  wire or_1_out, or_2_out;

  or or_1 (or_1_out, I3, I2);
  or or_2 (or_2_out, I1, I0);
  or or_3 (Y1, I3, I1);
  or or_4 (Y2, I3, I2);
  or or_5 (V, or_1_out, or_2_out);
endmodule
