// Logisim project [디지털시스템설계]실습_4주차_201413283_김재훈.circ as structural Verilog: 4 circuits, main circuit main
module main (
  input  S1,
  input  S0,
  input  S1_2,
  input  S0_2,
  input  D3,
  input  D2,
  input  D1,
  input  D0,
  output O3,
  output O2,
  output O1,
  output O0
);

  wire mux_1_f;

  mux mux_1 (.D3(D3), .D2(D2), .D1(D1), .D0(D0), .S1(S1), .S0(S0), .f(mux_1_f));
  demux demux_1 (.I(mux_1_f), .S1(S1_2), .S0(S0_2), .O3(O3), .O2(O2), .O1(O1), .O0(O0));
endmodule

module mux (
  input  S1,
  input  S0,
  input  D3,
  input  D2,
  input  D1,
  input  D0,
  output f
);

  wire and_1_out, and_2_out, and_3_out, and_4_out, not_1_out, not_2_out;

  not not_1 (not_1_out, S1);
  not not_2 (not_2_out, S0);
  and and_1 (and_1_out, not_2_out, not_1_out, D3);
  and and_2 (and_2_out, S0, not_1_out, D2);
  and and_3 (and_3_out, not_2_out, S1, D1);
  and and_4 (and_4_out, S0, S1, D0);
  or or_1 (f, and_1_out, and_2_out, and_3_out, and_4_out);
endmodule

module demux (
  input  S1,
  input  S0,
  input  I,
  output O3,
  output O2,
  output O1,
  output O0
);

  wire not_1_out, not_2_out;

  not not_1 (not_1_out, S1);
  not not_2 (not_2_out, S0);
  and and_1 (O3, not_1_out, not_2_out, I);
  and and_2 (O2, S0, not_1_out, I);
  and and_3 (O1, S1, not_2_out, I);
  and and_4 (O0, S0, S1, I);
endmodule

module _2 (
  input  D,
  output Q,
  output Q_prime
);

  wire CLK_out, nand_1_out, nand_2_out, nand_3_out, nand_4_out, nand_5_out, nand_6_out, not_1_out, not_2_out;

  not not_1 (not_1_out, D);
  not not_2 (not_2_out, CLK_out);
  Clock CLK (.out(CLK_out));
  nand nand_1 (nand_1_out, D, not_2_out);
  nand nand_2 (nand_2_out, not_2_out, not_1_out);
  nand nand_3 (nand_3_out, nand_1_out, nand_4_out);
  nand nand_4 (nand_4_out, nand_3_out, nand_2_out);
  nand nand_5 (nand_5_out, nand_3_out, CLK_out);
  nand nand_6 (nand_6_out, nand_4_out, CLK_out);
  nand nand_7 (Q, nand_5_out, Q_prime);
  nand nand_8 (Q_prime, Q, nand_6_out);
endmodule
