// Logisim project 5주차 실습_201413283_김재훈.circ as structural Verilog: 2 circuits, main circuit main
module main (
  input  Count_Signal,
  output Q3,
  output Q2,
  output Q1,
  output Q0
);

  wire and_1_out, and_2_out, and_3_out, CLK_out;

  Clock CLK (.out(CLK_out));
  and and_1 (and_1_out, and_2_out, Q2);
  and and_2 (and_2_out, and_3_out, Q1);
  and and_3 (and_3_out, Count_Signal, Q0);
  J_K_Flip_Flop j_k_ff_1 (.J(and_1_out), .clk(CLK_out), .K(and_1_out), .Q(Q3));  // open: Qn, preset, en, reset
  J_K_Flip_Flop j_k_ff_2 (.J(and_2_out), .clk(CLK_out), .K(and_2_out), .Q(Q2));  // open: Qn, preset, en, reset
  J_K_Flip_Flop j_k_ff_3 (.J(and_3_out), .clk(CLK_out), .K(and_3_out), .Q(Q1));  // open: Qn, preset, en, reset
  J_K_Flip_Flop j_k_ff_4 (.J(Count_Signal), .clk(CLK_out), .K(Count_Signal), .Q(Q0));  // open: Qn, preset, en, reset
endmodule

module _2 (
  input  \R_입력신호 ,
  input  \R_제어신호 ,
  input  \L_입력신호 ,
  input  \L_제어신호 ,
  output A,
  output B,
  output C,
  output D
);

  wire and_1_out, and_2_out, and_3_out, and_4_out, and_5_out, and_6_out, and_7_out, and_8_out, CLK_out,
       or_1_out, or_2_out, or_3_out, or_4_out;

  Clock CLK (.out(CLK_out));
  or or_1 (or_1_out, and_1_out, and_2_out);
  and and_1 (and_1_out, \L_제어신호 , \L_입력신호 );
  D_Flip_Flop d_ff_1 (.clk(CLK_out), .D(or_1_out), .Q(A));  // open: Qn, preset, en, reset
  and and_2 (and_2_out, \R_제어신호 , B);
  D_Flip_Flop d_ff_2 (.clk(CLK_out), .D(or_2_out), .Q(B));  // open: Qn, preset, en, reset
  or or_2 (or_2_out, and_4_out, and_3_out);
  and and_3 (and_3_out, \R_제어신호 , C);
  and and_4 (and_4_out, \L_제어신호 , A);
  or or_3 (or_3_out, and_5_out, and_6_out);
  and and_5 (and_5_out, \L_제어신호 , B);
  D_Flip_Flop d_ff_3 (.clk(CLK_out), .D(or_3_out), .Q(C));  // open: Qn, preset, en, reset
  and and_6 (and_6_out, \R_제어신호 , D);
  or or_4 (or_4_out, and_8_out, and_7_out);
  and and_7 (and_7_out, \R_제어신호 , \R_입력신호 );
  and and_8 (and_8_out, \L_제어신호 , C);
  D_Flip_Flop d_ff_4 (.clk(CLK_out), .D(or_4_out), .Q(D));  // open: Qn, preset, en, reset
endmodule
